// Logisim project add.circ as structural Verilog: 1 circuit, main circuit main
module main (
  input  A0,
  input  A1,
  input  A2,
  input  A3,
  input  B0,
  input  B1,
  input  B2,
  input  B3,
  output out_9,
  output out_10,
  output out_11,
  output out_12
);

  wire adder_1_cout, adder_2_cout, adder_3_cout;

  Adder #(.width(1)) adder_1 (.a(A0), .b(B0), .out(out_9), .cin(1'b0), .cout(adder_1_cout));
  Adder #(.width(1)) adder_2 (.a(A1), .b(B1), .out(out_10), .cin(adder_1_cout), .cout(adder_2_cout));
  Adder #(.width(1)) adder_3 (.a(A2), .b(B2), .out(out_11), .cin(adder_2_cout), .cout(adder_3_cout));
  Adder #(.width(1)) adder_4 (.a(A3), .b(B3), .out(out_12), .cin(adder_3_cout));  // open: cout
endmodule
