// Logisim project alu.circ as structural Verilog: 1 circuit, main circuit main
module main (
  input  A0,
  input  A1,
  input  A2,
  input  A3,
  input  B0,
  input  B1,
  input  B2,
  input  CLOCK,
  input  B3,
  input  in_10,
  input  S1,
  input  S2,
  input  in_13,
  output out_14,
  output out_15,
  output out_16,
  output out_17
);

  wire multiplexer_2_out, multiplexer_3_out, multiplexer_4_out, multiplexer_5_out;
  wire [3:0] main_1_out_9, main_2_o1, main_3_o1, main_4_o1, main_5_out_9, main_6_o1, multiplexer_1_out;

  add_main main_1 (
    .A0(A0), .A1(A1), .A2(A2), .A3(A3), .B0(B0), .B1(B1), .B2(B2), .B3(B3), .out_9(main_1_out_9[0]),
    .out_10(main_1_out_9[1]), .out_11(main_1_out_9[2]), .out_12(main_1_out_9[3]));
  or_main main_2 (
    .A1(A0), .A2(A1), .A3(A2), .A4(A3), .B1(B0), .B2(B1), .B3(B2), .B4(B3), .O1(main_2_o1[0]),
    .O2(main_2_o1[1]), .O3(main_2_o1[2]), .O4(main_2_o1[3]));
  and_main main_3 (
    .A1(A0), .A2(A1), .A3(A2), .A4(A3), .B1(B0), .B2(B1), .B3(B2), .B4(B3), .O1(main_3_o1[0]),
    .O2(main_3_o1[1]), .O3(main_3_o1[2]), .O4(main_3_o1[3]));
  xor_main main_4 (
    .A1(A0), .A2(A1), .A3(A2), .A4(A3), .B1(B0), .B2(B1), .B3(B2), .B4(B3), .O1(main_4_o1[0]),
    .O2(main_4_o1[1]), .O3(main_4_o1[2]), .O4(main_4_o1[3]));
  sub_main main_5 (
    .A0(A0), .A1(A1), .A2(A2), .A3(A3), .in_5(B0), .B1(B1), .B2(B2), .B3(B3), .out_9(main_5_out_9[0]),
    .out_10(main_5_out_9[1]), .out_11(main_5_out_9[2]), .out_12(main_5_out_9[3]));
  not_main main_6 (
    .A1(A0), .A2(A1), .A3(A2), .A4(A3), .B1(B0), .B2(B1), .B3(B2), .B4(B3), .O1(main_6_o1[0]),
    .O2(main_6_o1[1]), .O3(main_6_o1[2]), .O4(main_6_o1[3]));
  Multiplexer #(.select(3), .width(4)) multiplexer_1 (
    .in0(main_1_out_9), .in1(main_2_o1), .in2(main_3_o1), .in3(main_4_o1), .in4(main_5_out_9),
    .in5(main_6_o1), .out(multiplexer_1_out), .sel({in_13, S2, S1}));  // open: in6, in7, en
  Multiplexer multiplexer_2 (
    .in0(out_14), .in1(multiplexer_1_out[0]), .out(multiplexer_2_out), .sel(in_10));  // open: en
  Multiplexer multiplexer_3 (
    .in0(out_15), .in1(multiplexer_1_out[1]), .out(multiplexer_3_out), .sel(in_10));  // open: en
  Multiplexer multiplexer_4 (
    .in0(out_16), .in1(multiplexer_1_out[2]), .out(multiplexer_4_out), .sel(in_10));  // open: en
  Multiplexer multiplexer_5 (
    .in0(out_17), .in1(multiplexer_1_out[3]), .out(multiplexer_5_out), .sel(in_10));  // open: en
  D_Flip_Flop d_ff_1 (.clk(CLOCK), .D(multiplexer_2_out), .Q(out_14));  // open: Qn, preset, en, reset
  D_Flip_Flop d_ff_2 (.clk(CLOCK), .D(multiplexer_3_out), .Q(out_15));  // open: Qn, preset, en, reset
  D_Flip_Flop d_ff_3 (.clk(CLOCK), .D(multiplexer_4_out), .Q(out_16));  // open: Qn, preset, en, reset
  D_Flip_Flop d_ff_4 (.clk(CLOCK), .D(multiplexer_5_out), .Q(out_17));  // open: Qn, preset, en, reset

  // Notes on the sheet:
  //   ADD
  //   OR
  //   AND
  //   XOR
  //   SUB
  //   not
  //   S0
  //   ENABLE
  //   4 BIT REG
endmodule
