// Logisim project not.circ as structural Verilog: 1 circuit, main circuit main
module main (
  input  A1,
  input  A2,
  input  A3,
  input  A4,
  input  B1,
  input  B2,
  input  B3,
  input  B4,
  output O1,
  output O2,
  output O3,
  output O4
);

  not not_1 (O1, A1);
  not not_2 (O2, A2);
  not not_3 (O3, A3);
  not not_4 (O4, A4);

  // Notes on the sheet:
  //   NOT
  //   no need to connect B part
endmodule
