// Logisim project xor.circ as structural Verilog: 1 circuit, main circuit main
module main (
  input  A1,
  input  A2,
  input  A3,
  input  A4,
  input  B1,
  input  B2,
  input  B3,
  input  B4,
  output O1,
  output O2,
  output O3,
  output O4
);

  xor xor_1 (O1, A1, B1);
  xor xor_2 (O2, A2, B2);
  xor xor_3 (O3, A3, B3);
  xor xor_4 (O4, A4, B4);

  // Notes on the sheet:
  //   XOR
endmodule
